# Fritzing sketch afficheurCathodeShema (saved by Fritzing 0.9.3b)
breadboards: 1

parts:
  Part1 = Arduino Mega 2560 (Rev3)
  R1 = Resistor [tolerance=±5% resistance=150k package=THT]
  R2 = Resistor [tolerance=±5% resistance=150k package=THT]
  R3 = Resistor [tolerance=±5% resistance=150k package=THT]
  R4 = Resistor [tolerance=±5% resistance=150k package=THT]
  R5 = Resistor [tolerance=±5% resistance=150k package=THT]
  R6 = Resistor [tolerance=±5% resistance=150k package=THT]
  R7 = Resistor [tolerance=±5% resistance=150k package=THT]
  7_Segment1 = 7 Segment Display
  R8 = Resistor [tolerance=±5% resistance=150k package=THT]

nets:
  N1: Part1.D11_PWM, R8.Pin_0
  N2: Part1.D10_PWM, R4.Pin_0
  N3: Part1.D9_PWM, R5.Pin_0
  N4: Part1.D8_PWM, R1.Pin_0
  N5: Part1.5V, 7_Segment1.common_cathode#3, 7_Segment1.common_cathode#5, 7_Segment1.common_cathode#11, 7_Segment1.common_cathode#16
  N6: Part1.D4_PWM, R3.Pin_0
  N7: Part1.D5_PWM, R6.Pin_0
  N8: Part1.D6_PWM, R2.Pin_0
  N9: Part1.D7_PWM, R7.Pin_0
  N10: R1.Pin_1, 7_Segment1.Segment_E
  N11: R2.Pin_1, 7_Segment1.Segment_F
  N12: R3.Pin_1, 7_Segment1.Segment_A
  N13: R4.Pin_1, 7_Segment1.Segment_D
  N14: R5.Pin_1, 7_Segment1.common_cathode#12
  N15: R6.Pin_1, 7_Segment1.Segment_B
  N16: R7.Pin_1, 7_Segment1.Segment_G
  N17: 7_Segment1.Segment_DP, R8.Pin_1
